# Fritzing sketch bitLovePlant (saved by Fritzing 0.9.4)

parts:
  R1 = BBC MicroBit
  Componente1 = FC-28 Soil Hygrometer Module - Probe
  Componente2 = FC-28 Soil Hygrometer Module
  YL-83_-_Detection_Board1 = YL-83 Rain Sensor - Detection Board
  Componente3 = FC-28 Soil Hygrometer Module
  M1 = DC Motor  # not connected
  2_Channel_Relay1 = 2 Channel Power Relay
  BATT1 = 4xAA Switchable Battery Pack w/JST connector
  Water_Level_Sensor1 = Water Level Sensor

nets:
  GND: R1.GND, Componente2.GND, Componente3.GND, 2_Channel_Relay1.GND, Water_Level_Sensor1.GND
  VCC: R1.3v3, Componente2.VCC, Componente3.VCC, 2_Channel_Relay1.VCC, Water_Level_Sensor1.VCC
  N1: R1.P16, 2_Channel_Relay1.IN1
  N2: R1.P2_-_ANALOG_IN, Water_Level_Sensor1.SIG
  N3: R1.P1_ANALOG_IN, Componente3.AO
  N4: R1.P0_ANALOG_IN, Componente2.AO
  N5: Componente1.POS, Componente2.POS
  N6: Componente1.NEG, Componente2.NEG
  N7: YL-83_-_Detection_Board1.POS, Componente3.POS
  N8: YL-83_-_Detection_Board1.NEG, Componente3.NEG
  N9: 2_Channel_Relay1.K2-COM, BATT1.POS

custom parts:
  BBC MicroBit: The BBC MICRO:BIT
  FC-28 Soil Hygrometer Module - Probe: The FC-28 is a soil hygrometer module that uses the Texas Instruments LM393 comparator chip to provide an analog measurement of soil humidity.
  FC-28 Soil Hygrometer Module: The FC-28 is a soil hygrometer module that uses the Texas Instruments LM393 comparator chip to provide an analog measurement of soil humidity. The digital output is high when soil moisture is over a certain threshold, as determined by adjusting the potentiometer.
  YL-83 Rain Sensor - Detection Board: The YL-83 is a rain sensor that has more resistance when dry and less resistance when wet. The module runs at 5V.
  2 Channel Power Relay: A 2 channel power relay. The module operates at 5V.
  4xAA Switchable Battery Pack w/JST connector: 4xAA Switchable Battery Pack with JST connector
  Water Level Sensor: A water level sensor. This sensor operates at 3V to 5V. The Sig (signal) pin outputs an analogue signal that is in proportion to the amount of water in contact with the sensor.
